# Fritzing sketch goldibox (saved by Fritzing 0.9.2b)
circuit board: 3.26877cm x 1.7006cm
circuit board: 2.5cm x 1.5cm
perfboards: 2

parts:
  J1_Peltier = Peltier Element
  F1_Fan_12VDC = Fan - Ventilador [package=THT]
  R16 = Resistor [tolerance=±5% resistance=4.7k package=THT]
  R17 = Resistor [tolerance=±5% resistance=1k package=THT]
  C16 = Electrolytic Capacitor [capacitance=10µF package="100 mil [THT, electrolytic]"]
  Therm1_int = Temperature Sensor (Thermistor) [thermistor_type=NTC package=THT]
  R19 = Resistor [tolerance=±5% resistance=4.7k package=THT]
  R20 = Resistor [tolerance=±5% resistance=1k package=THT]
  C17 = Electrolytic Capacitor [capacitance=10µF package="100 mil [THT, electrolytic]"]
  Therm2_ext = Temperature Sensor (Thermistor) [thermistor_type=NTC package=THT]
  C23 = Ceramic Capacitor [capacitance=100nF voltage=20V package="100 mil [THT, multilayer]"]
  C24 = Ceramic Capacitor [capacitance=100nF package="100 mil [THT, multilayer]"]
  Part2 = IRF540 MOSFET module
  PocketBeagle = PocketBeagle
  J1 = male pin header, 2 pins [form="♂ (male)"]
  J2 = female pin header, 2 pins [form="♀ (female)"]
  J3 = male pin header, 2 pins [form="♂ (male)"]
  J12 = female pin header, 1 pin [form="♀ (female)"]
  J11 = female pin header, 1 pin [form="♀ (female)"]
  J4 = female pin header, 2 pins [form="♀ (female)"]
  J18 = female pin header, 3 pins [form="♀ (female)"]
  J19 = female pin header, 6 pins [form="♀ (female)"]
  S2_** = H-Bridge with L298N v2
  J20-HBr = male pin header, 3 pins [form="♂ (male)"]
  J14 = male pin header, 4 pins [form="♂ (male)"]
  J13 = female pin header, 4 pins [form="♀ (female)"]
  J8 = female alternating pin header, 3 pins [form="♀ (female)"]
  J7-AIN = male pin header, 3 pins [form="♂ (male)"]
  J21-USB = male pin header, 6 pins [form="♂ (male)"]
  J22-UART = male pin header, 1 pin [form="♂ (male)"]
  J22-UART_2 = male pin header, 2 pins [form="♂ (male)"]
  JP2--PB_power = USB_MICROB_PLUG [package=micro-b-ra-th]
  5VDC_VReg = VERTER 5V USB Buck-Boost
  J23-LEDs = male pin header, 5 pins [form="♂ (male)"]
  J24 = female alternating pin header, 5 pins [form="♀ (female)"]
  LED1 = smd LED [color="Red (633nm)" package="1206 [SMD]"]
  LED2 = smd LED [color="Green (560nm)" package="1206 [SMD]"]
  LED3 = smd LED [color="Blue (470nm)" package="1206 [SMD]"]
  R21 = Resistor [tolerance=±5% resistance=470 package=THT]
  R22 = Resistor [tolerance=±5% resistance=470 package=THT]
  R23 = Resistor [tolerance=±5% resistance=470 package=THT]
  J9-Fan = male pin header, 2 pins [form="♂ (male)"]

nets:
  N1: J1_Peltier.pin1, S2_**.OUT2, S2_**.OUT3
  N2: J1_Peltier.pin2, S2_**.OUT1, S2_**.OUT4
  N3: F1_Fan_12VDC.5V, Part2.Vout+
  N4: F1_Fan_12VDC.GND, Part2.Vout-
  N5: R16.Pin_0, R17.Pin_0, J1.pin1
  N6: R16.Pin_1, C16.+, C24.1, J14.pin3
  N7: R17.Pin_1, R20.Pin_1, J14.pin1
  N8: C16.-, C17.-, C23.0, C24.0, J1.pin2, J3.pin2, J14.pin2
  N9: Therm1_int.pin_0, J2.pin1
  N10: Therm1_int.pin_1, J2.pin2
  N11: R19.Pin_0, R20.Pin_0, J3.pin1
  N12: R19.Pin_1, C17.+, C23.1, J14.pin4
  N13: Therm2_ext.pin_0, J4.pin1
  N14: Therm2_ext.pin_1, J4.pin2
  5V: Part2.V+, S2_**.+VSS
  GND: Part2.V-, Part2.Vin-, PocketBeagle.GND, S2_**.GND, J21-USB.pin6, J22-UART.pin1, JP2--PB_power.GND, 5VDC_VReg.GND, J23-LEDs.pin5
  FAN: Part2.S, J12.pin1
  12V: Part2.Vin+, S2_**.+VS, 5VDC_VReg.VIN
  N15: PocketBeagle.AIN6/GPIO87, J20-HBr.pin1
  N16: PocketBeagle.GPIO89, J20-HBr.pin2
  N17: PocketBeagle.USB1.VBUS, J21-USB.pin1
  ENA/B: PocketBeagle.SPI0.CS, J20-HBr.pin3
  N18: PocketBeagle.USB1.VIN, J21-USB.pin2
  N19: PocketBeagle.SPI0.CLK, J23-LEDs.pin1
  N20: PocketBeagle.USB1.DN, J21-USB.pin3
  N21: PocketBeagle.SPI0.MISO, J23-LEDs.pin2
  N22: PocketBeagle.USB1.DP, J21-USB.pin4
  N23: PocketBeagle.SPI0.MOSI, J23-LEDs.pin3
  N24: PocketBeagle.USB1.ID, J21-USB.pin5
  3.3V: PocketBeagle.3.3V, J23-LEDs.pin4
  N25: PocketBeagle.AIN.VREFN, J7-AIN.pin1
  N26: PocketBeagle.AIN.VREFP, J9-Fan.pin1
  N27: PocketBeagle.AIN0(1.8V), J7-AIN.pin2
  N28: PocketBeagle.GPIO20, J9-Fan.pin2
  N29: PocketBeagle.AIN1(1.8V), J7-AIN.pin3
  N30: PocketBeagle.UART0.TX, J22-UART_2.pin1
  N31: PocketBeagle.UART0.RX, J22-UART_2.pin2
  N32: J11.pin1, J13.pin1
  N33: J18.pin1, J19.pin3, J19.pin4
  N34: J18.pin2, J19.pin2, J19.pin5
  N35: J18.pin3, J19.pin1, J19.pin6
  N36: J13.pin2, J8.pin1
  N37: J13.pin3, J8.pin2
  N38: J13.pin4, J8.pin3
  N39: JP2--PB_power.VCC, 5VDC_VReg.5.0V
  N40: J24.pin1, R23.Pin_0
  N41: J24.pin2, R22.Pin_0
  N42: J24.pin3, R21.Pin_0
  N43: J24.pin5, LED1.cathode, LED2.cathode, LED3.cathode
  N44: LED1.anode, R21.Pin_1
  N45: LED2.anode, R22.Pin_1
  N46: LED3.anode, R23.Pin_1

notes:
  Configure both L298N 2A bridges in parallel for 4A Peltier
  Goldibox, Not too hot, not too cold.  See https://github.com/zultron/goldibox, 0.1
  ** onboard 5V reg
  12VDC in
  USB breakout
  optional serial
  console
  for WiFi

custom parts:
  Fan - Ventilador: Ventilador de 2 pines, se encuentra comunmente en computadoras de escritorio
  H-Bridge with L298N v2: h-bridge
  VERTER 5V USB Buck-Boost: VERTER can take battery voltages from 3-12VDC and output a nice 5V DC, which makes it a perfect universal power supply for your portable project! Where Verter really shines is when you have a battery or power range that can fluctuate a lot, or you don't know what you'll end up using.
