# Fritzing sketch incubator (saved by Fritzing 0.9.2b)
circuit board: 4cm x 3.23893cm
perfboards: 1

parts:
  J1_Peltier = Peltier Element
  F1_Fan_12VDC = Fan - Ventilador [package=THT]
  12VDC_in = 2.1mm Barrel Jack with Terminal Block
  S2_** = H-Bridge with L298N v2
  R16 = Resistor [tolerance=±5% resistance=4.7k package=THT]
  R17 = Resistor [tolerance=±5% resistance=2.0k package=THT]
  C16 = Electrolytic Capacitor [capacitance=10µF package="100 mil [THT, electrolytic]"]
  100k_Therm1 = Temperature Sensor (Thermistor) [thermistor_type=NTC package=THT]
  R19 = Resistor [tolerance=±5% resistance=4.7k package=THT]
  R20 = Resistor [tolerance=±5% resistance=2.0k package=THT]
  C17 = Electrolytic Capacitor [capacitance=10µF package="100 mil [THT, electrolytic]"]
  100k_Therm2 = Temperature Sensor (Thermistor) [thermistor_type=NTC package=THT]
  R22 = Resistor [tolerance=±5% resistance=4.7k package=THT]
  R23 = Resistor [tolerance=±5% resistance=2.0k package=THT]
  C19 = Electrolytic Capacitor [capacitance=10µF package="100 mil [THT, electrolytic]"]
  100k_Therm3 = Temperature Sensor (Thermistor) [thermistor_type=NTC package=THT]
  C23 = Ceramic Capacitor [capacitance=100nF voltage=20V package="100 mil [THT, multilayer]"]
  C24 = Ceramic Capacitor [capacitance=100nF package="100 mil [THT, multilayer]"]
  C25 = Ceramic Capacitor [capacitance=100nF package="100 mil [THT, multilayer]"]
  Part2 = IRF540 MOSFET module
  PocketBeagle = PocketBeagle
  J1 = male pin header, 2 pins [form="♂ (male)"]
  J2 = female pin header, 2 pins [form="♀ (female)"]
  J4 = male pin header, 2 pins [form="♂ (male)"]
  J5 = female pin header, 2 pins [form="♀ (female)"]
  J6 = male pin header, 2 pins [form="♂ (male)"]
  J7 = male pin header, 5 pins [form="♂ (male)"]
  J12 = female pin header, 5 pins [form="♀ (female)"]
  J14 = male pin header, 1 pin [form="♂ (male)"]
  J15 = female pin header, 1 pin [form="♀ (female)"]
  J16 = male pin header, 3 pins [form="♂ (male)"]
  J19 = female pin header, 1 pin [form="♀ (female)"]
  J21 = female pin header, 1 pin [form="♀ (female)"]
  J8 = male pin header, 4 pins [form="♂ (male)"]
  J10 = male pin header, 3 pins [form="♂ (male)"]
  J24 = female pin header, 4 pins [form="♀ (female)"]
  J25 = female pin header, 1 pin [form="♀ (female)"]
  J3 = female pin header, 2 pins [form="♀ (female)"]
  J17 = female pin header, 3 pins [form="♀ (female)"]
  J18 = female pin header, 6 pins [form="♀ (female)"]
  J26 = male pin header, 6 pins [form="♂ (male)"]

nets:
  N1: J1_Peltier.pin1, S2_**.OUT2, S2_**.OUT3
  N2: J1_Peltier.pin2, S2_**.OUT1, S2_**.OUT4
  N3: F1_Fan_12VDC.5V, Part2.Vout+
  N4: F1_Fan_12VDC.GND, Part2.Vout-
  12V: 12VDC_in.POS, S2_**.+VS, Part2.Vin+
  GND: 12VDC_in.NEG, S2_**.GND, Part2.V-, Part2.Vin-, PocketBeagle.GND, J19.pin1, J10.pin3
  5VCC: S2_**.+VSS, Part2.V+, J15.pin1
  N5: S2_**.ENA, J26.pin1
  N6: S2_**.IN1, J26.pin2
  N7: S2_**.IN2, J26.pin3
  N8: S2_**.IN3, J26.pin4
  N9: S2_**.IN4, J26.pin5
  N10: S2_**.ENB, J26.pin6
  N11: R16.Pin_0, R17.Pin_0, J1.pin1
  N12: R16.Pin_1, C16.+, C24.1, J7.pin3
  N13: R17.Pin_1, R20.Pin_1, R23.Pin_1, J7.pin1
  N14: C16.-, C17.-, C19.-, C23.0, C24.0, C25.0, J1.pin2, J4.pin2, J6.pin2, J7.pin2
  N15: 100k_Therm1.pin_0, J2.pin1
  N16: 100k_Therm1.pin_1, J2.pin2
  N17: R19.Pin_0, R20.Pin_0, J4.pin1
  N18: R19.Pin_1, C17.+, C23.1, J7.pin4
  N19: 100k_Therm2.pin_0, J3.pin1
  N20: 100k_Therm2.pin_1, J3.pin2
  N21: R22.Pin_0, R23.Pin_0, J6.pin1
  N22: R22.Pin_1, C19.+, C25.1, J7.pin5
  N23: 100k_Therm3.pin_0, J5.pin1
  N24: 100k_Therm3.pin_1, J5.pin2
  FAN: Part2.S, J21.pin1
  N25: PocketBeagle.VIN, J14.pin1
  N26: PocketBeagle.AIN.VREFN, J8.pin1
  N27: PocketBeagle.AIN.VREFP, J10.pin1
  N28: PocketBeagle.AIN0(1.8V), J8.pin2
  N29: PocketBeagle.GPIO20, J10.pin2
  N30: PocketBeagle.AIN1(1.8V), J8.pin3
  N31: PocketBeagle.AIN2(1.8V), J8.pin4
  N32: PocketBeagle.GPIO59, J16.pin1
  N33: PocketBeagle.GPIO58, J16.pin2
  N34: PocketBeagle.GPIO57, J16.pin3
  N35: J12.pin1, J25.pin1
  N36: J12.pin2, J24.pin1
  N37: J12.pin3, J24.pin2
  N38: J12.pin4, J24.pin3
  N39: J12.pin5, J24.pin4
  N40: J17.pin1, J18.pin1, J18.pin6
  N41: J17.pin2, J18.pin2, J18.pin5
  N42: J17.pin3, J18.pin3, J18.pin4

notes:
  Configure both L298N 2A bridges in parallel for 4A Peltier
  Only Therm1 in use; others for future expansion
  Goldilocks Incubator, Not too hot, not too cold.  See https://github.com/zultron/goldilocks-incubator, 0.1
  ** has onboard 5V reg

custom parts:
  Fan - Ventilador: Ventilador de 2 pines, se encuentra comunmente en computadoras de escritorio
  H-Bridge with L298N v2: h-bridge
