# Fritzing sketch incubator (saved by Fritzing 0.9.2b)
circuit board: 3.132cm x 3.23893cm
breadboards: 1

parts:
  R1_100K_therm = Temperature Sensor (Thermistor) [thermistor_type=NTC package=THT]
  J1_Peltier = Peltier Element
  F1_Fan_12VDC = Fan - Ventilador [package=THT]
  12VDC_in = 2.1mm Barrel Jack with Terminal Block
  BeagleBone1 = BeagleBone Black V3
  R3 = Resistor [tolerance=±5% resistance=4.7k package=THT]
  C2 = Electrolytic Capacitor [capacitance=10µF package="100 mil [THT, electrolytic]"]
  C1 = Ceramic Capacitor [capacitance=100nF package="100 mil [THT, multilayer]"]
  R2 = Resistor [tolerance=±5% resistance=2.0k package=THT]
  S2 = H-Bridge with L298N v2
  5VDC_out_to_BeagleBone = 2.1mm Barrel Jack with Terminal Block

nets:
  N1: R1_100K_therm.pin_0, BeagleBone1.P9.34, C2.-, C1.1
  N2: R1_100K_therm.pin_1, R3.Pin_1, R2.Pin_0
  N3: J1_Peltier.pin1, S2.OUT2
  N4: J1_Peltier.pin2, S2.OUT1
  N5: F1_Fan_12VDC.5V, S2.OUT4
  N6: F1_Fan_12VDC.GND, S2.OUT3
  N7: 12VDC_in.POS, S2.+VS
  N8: 12VDC_in.NEG, S2.GND, 5VDC_out_to_BeagleBone.NEG
  N9: BeagleBone1.P9.32, R2.Pin_1
  N10: BeagleBone1.P9.36, R3.Pin_0, C2.+, C1.0
  N11: BeagleBone1.P8.08, S2.ENA
  N12: BeagleBone1.P8.10, S2.IN1
  N13: BeagleBone1.P8.12, S2.IN2
  N14: BeagleBone1.P8.14, S2.IN3
  N15: BeagleBone1.P8.16, S2.IN4
  N16: BeagleBone1.P8.18, S2.ENB
  N17: S2.+VSS, 5VDC_out_to_BeagleBone.POS

custom parts:
  Fan - Ventilador: Ventilador de 2 pines, se encuentra comunmente en computadoras de escritorio
  BeagleBone Black V3: BeagleBone Black rev. A5B
  H-Bridge with L298N v2: h-bridge
